# Fritzing sketch 328p (saved by Fritzing 0.9.3b)
breadboards: 1

parts:
  J1 = Dagu DGServo 9g header (male) [package=THT]
  J2 = Dagu DGServo 9g header (male) [package=THT]
  J3 = Dagu DGServo 9g header (male) [package=THT]
  J4 = Dagu DGServo 9g header (male) [package=THT]
  J5 = Dagu DGServo 9g header (male) [package=THT]
  J6 = Dagu DGServo 9g header (male) [package=THT]
  U1 = atmega328 [package=dip]

nets:
  GND: J1.gnd, J2.gnd, J3.gnd, J4.gnd, J5.gnd, J6.gnd, U1.GND#7
