# Fritzing sketch RCtoI2C (saved by Fritzing 0.9.3b)
circuit board: 6.04506cm x 4.51435cm

parts:
  Part1 = Arduino Pro Mini v13
  J1 = Camdenboss CTB0158-2 [part_number=CTB0158-2 package=THT]
  J2 = Camdenboss CTB0158-2 [part_number=CTB0158-2 package=THT]
  J4 = male pin header, 7 pins [form="♂ (male)"]
  J5 = male pin header, 7 pins [form="♂ (male)"]
  J6 = male pin header, 7 pins [form="♂ (male)"]

nets:
  N1: Part1.VCC, J2.pin2, J6.pin7
  N2: Part1.GND, J2.pin1, J5.pin7
  N3: Part1.A4, J1.pin2
  N4: Part1.A5, J1.pin1
  N5: Part1.D9_PWM, J4.pin6
  N6: Part1.D8, J4.pin5
  N7: Part1.D7, J4.pin4
  N8: Part1.D6_PWM, J4.pin3
  N9: Part1.D5_PWM, J4.pin2
  N10: Part1.D4, J4.pin1

notes:
  RC to I2C converter
  - + S
